# Fritzing sketch AVR_ac_INTERNAL_test (saved by Fritzing 0.9.6b)
breadboards: 1

parts:
  Part1 = Arduino Uno (Rev3)
  R1 = Rotary Potentiometer (Small) [maximum_resistance=100kΩ package=THT]
  R2 = Resistor [tolerance=±5% resistance=330 power=0.25 package=THT]
  LED1 = LED - 5mm [color="Red (633nm)" current=0.030 package="5 mm [THT]"]
  R4 = Resistor [tolerance=±5% resistance=330 power=0.25 package=THT]
  LED2 = LED - 5mm [color="Green (555nm)" current=0.030 package="5 mm [THT]"]

nets:
  N1: Part1.D8, LED2.anode
  N2: Part1.D13/SCK, LED1.anode
  N3: Part1.GND, R1.leg1, R2.Pin_0, R4.Pin_0
  N4: Part1.D7, R1.wiper
  N5: Part1.5V, R1.leg2
  N6: R2.Pin_1, LED1.cathode
  N7: R4.Pin_1, LED2.cathode

notes:
  R1
  R1 = R2 = 330R
  VR1
  VR1 = 10K
  5V
  GND
  D8
  D13
  R2
  D7
