# Fritzing sketch AVR_ac_MUX_test (saved by Fritzing 0.9.3b)
breadboards: 1

parts:
  Part1 = Arduino Uno (Rev3)
  R1 = Rotary Potentiometer (Small) [maximum_resistance=100kΩ package=THT]
  R2 = Resistor [tolerance=±5% resistance=330 package=THT]
  LED1 = LED - 5mm [color="Red (633nm)" package="5 mm [THT]"]
  R4 = Resistor [tolerance=±5% resistance=330 package=THT]
  LED2 = LED - 5mm [color="Green (555nm)" package="5 mm [THT]"]

nets:
  N1: Part1.A3, R1.wiper
  N2: Part1.D8, LED2.anode
  N3: Part1.D13/SCK, LED1.anode
  N4: Part1.D6_PWM, Part1.3V3
  N5: Part1.5V, R1.leg2
  N6: Part1.GND, R1.leg1, R2.Pin_0, R4.Pin_0
  N7: R2.Pin_1, LED1.cathode
  N8: R4.Pin_1, LED2.cathode

notes:
  R1
  R1 = R2 = 330R
  VR1
  VR1 = 10K
  A3
  D6
  3.3V
  5V
  GND
  D8
  D13
  R2
